# Fritzing sketch comm_maitre_esclave (saved by Fritzing 0.9.3b)
circuit board: 11.6276cm x 12.4178cm

parts:
  Composant1 = Arduino Uno (Rev3) - ICSP
  Composant2 = Arduino Uno (Rev3) - ICSP

nets:
  N1: Composant1.A4/SDA, Composant2.A4/SDA
  N2: Composant1.A5/SCL, Composant2.A5/SCL
  5V: Composant1.5V, Composant2.VIN
  GND: Composant1.GND, Composant2.GND

notes:
  Arduino Esclave
  Arduino Maitre
