# Fritzing sketch esclave_motor (saved by Fritzing 0.9.3b)
circuit board: 11.6276cm x 12.4178cm

parts:
  Composant1 = Arduino Uno (Rev3) - ICSP
  Composant2 = Arduino Uno (Rev3) - ICSP
  Composant3 = Rotoshield - Motor driver shield for Arduino
  M2 = DC Motor
  M1 = DC Motor
  U1 = LIPO-1000mAh [package=lipo-1000]

nets:
  N1: Composant1.A4/SDA, Composant2.A4/SDA
  N2: Composant1.A5/SCL, Composant2.A5/SCL
  5V: Composant1.5V, Composant2.VIN
  GND: Composant1.GND, Composant2.GND
  N3: Composant3.M1-2, M1.pin_2
  N4: Composant3.M1-1, M1.pin_1
  N5: Composant3.M2-2, M2.pin_2
  N6: Composant3.M2-1, M2.pin_1
  N7: Composant3.VCC, U1.+
  N8: Composant3.GND, U1.-

notes:
  Arduino Esclave
  Avec
  shield Motor
  Arduino Maitre
