# Fritzing sketch maitre_sensor (saved by Fritzing 0.9.3b)
breadboards: 1

parts:
  hc-sr1 = hc-sr04
  hc-sr2 = hc-sr04
  hc-sr3 = hc-sr04
  hc-sr4 = hc-sr04
  hc-sr5 = hc-sr04
  Composant2 = Arduino Uno (Rev3) - ICSP
  hc-sr6 = hc-sr04

nets:
  VCC: hc-sr1.VCC, hc-sr2.VCC, hc-sr3.VCC, hc-sr4.VCC, hc-sr5.VCC, hc-sr6.VCC
  N1: hc-sr1.Trig, Composant2.D3_PWM
  N2: hc-sr1.Echo, Composant2.D2
  GND: hc-sr1.GND, hc-sr2.GND, hc-sr3.GND, hc-sr4.GND, hc-sr5.GND, hc-sr6.GND
  N3: hc-sr2.Trig, Composant2.D5_PWM
  N4: hc-sr2.Echo, Composant2.D4
  N5: hc-sr3.Trig, Composant2.D7
  N6: hc-sr3.Echo, Composant2.D6_PWM
  N7: hc-sr4.Trig, Composant2.D9_PWM
  N8: hc-sr4.Echo, Composant2.D8
  N9: hc-sr5.Trig, Composant2.D11_PWM/MOSI
  N10: hc-sr5.Echo, Composant2.D10_PWM/SS
  N11: Composant2.D12/MISO, hc-sr6.Echo
  N12: Composant2.D13/SCK, hc-sr6.Trig

notes:
  Sensor 1
  Sensor 2
  Sensor 3
  Sensor 4
  Sensor 5
  Arduino Maitre
  Sensor 6
