# Fritzing sketch scrappy (saved by Fritzing 0.9.3b)
breadboards: 1

parts:
  Composant1 = Arduino Uno (Rev3)  # not connected
  Composant2 = Rotoshield - Motor driver shield for Arduino
  M1 = DC Motor
  M2 = DC Motor
  hc-sr2 = hc-sr04
  hc-sr3 = hc-sr04
  hc-sr4 = hc-sr04
  hc-sr5 = hc-sr04
  hc-sr6 = hc-sr04
  hc-sr1 = hc-sr04

nets:
  N1: Composant2.DIG_2, hc-sr1.Echo
  N2: Composant2.DIG_3, hc-sr2.Echo
  N3: Composant2.DIG_4, hc-sr4.Echo
  N4: Composant2.DIG_5, hc-sr3.Echo
  N5: Composant2.DIG_6, hc-sr5.Echo
  N6: Composant2.DIG_7, hc-sr6.Echo
  N7: Composant2.DIG_8, hc-sr1.Trig
  N8: Composant2.DIG_9, hc-sr2.Trig
  N9: Composant2.DIG_10, hc-sr4.Trig
  N10: Composant2.DIG_11, hc-sr3.Trig
  N11: Composant2.DIG_12, hc-sr5.Trig
  N12: Composant2.DIG_13, hc-sr6.Trig
  VCC: Composant2.+5V, hc-sr2.VCC, hc-sr3.VCC, hc-sr4.VCC, hc-sr5.VCC, hc-sr6.VCC, hc-sr1.VCC
  GND: Composant2.GND, hc-sr2.GND, hc-sr3.GND, hc-sr4.GND, hc-sr5.GND, hc-sr6.GND, hc-sr1.GND
  N13: Composant2.M1-2, M1.pin_1
  N14: Composant2.M1-1, M1.pin_2
  N15: Composant2.M2-2, M2.pin_2
  N16: Composant2.M2-1, M2.pin_1

notes:
  | Emetteur
  GND
  OUT / DATA
  VCC
  Shield Motor
  connecté à un
  Arduino
  Source d'alimentation avec des piles
  5 piles de 1,2 V dans notre cas
  GND
  VCC
