# Fritzing sketch scrappy_junior (saved by Fritzing 0.9.3b)

parts:
  Composant1 = Arduino Uno (Rev3)  # not connected
  Composant2 = Rotoshield - Motor driver shield for Arduino
  hc-sr1 = hc-sr04
  M1 = DC Motor
  M2 = DC Motor

nets:
  N1: Composant2.DIG_3, hc-sr1.Echo
  N2: Composant2.DIG_4, hc-sr1.Trig
  +5V: Composant2.+5V, hc-sr1.VCC
  GND: Composant2.GND, hc-sr1.GND
  N3: Composant2.M1-2, M1.pin_2
  N4: Composant2.M1-1, M1.pin_1
  N5: Composant2.M2-2, M2.pin_2
  N6: Composant2.M2-1, M2.pin_1

notes:
  | Récepteur
  GND OUT / DATA VCC
  Source d'alimentation avec des piles
  5 piles de 1,2 V dans notre cas
  GND
  VCC
  Shield Motor
  connecté à un
  Arduino
