# Fritzing sketch sketch_ter (saved by Fritzing 0.9.3b)
breadboards: 1

parts:
  Composant1 = Arduino Uno (Rev3) - ICSP
  hc-sr1 = hc-sr04
  hc-sr2 = hc-sr04
  hc-sr3 = hc-sr04
  hc-sr4 = hc-sr04
  hc-sr5 = hc-sr04

nets:
  N1: Composant1.D8, hc-sr3.Echo
  N2: Composant1.D9_PWM, hc-sr3.Trig
  N3: Composant1.D11_PWM/MOSI, hc-sr5.Trig
  N4: Composant1.D12/MISO, hc-sr5.Echo
  N5: Composant1.D2, hc-sr1.Echo
  N6: Composant1.D3_PWM, hc-sr1.Trig
  N7: Composant1.D4, hc-sr2.Echo
  N8: Composant1.D5_PWM, hc-sr2.Trig
  N9: Composant1.D6_PWM, hc-sr4.Trig
  N10: Composant1.D7, hc-sr4.Echo
  VCC: Composant1.5V, hc-sr1.VCC, hc-sr2.VCC, hc-sr3.VCC, hc-sr4.VCC, hc-sr5.VCC
  GND: Composant1.GND, hc-sr1.GND, hc-sr2.GND, hc-sr3.GND, hc-sr4.GND, hc-sr5.GND

notes:
  Sensor 1
  Sensor 2
  Sensor 3
  Sensor 4
  Sensor 5
  Sensor 6
  Arduino UNO
